# Fritzing sketch LilyPicoFritzBuzzer (saved by Fritzing 0.9.10b)
breadboards: 2

parts:
  A1 = Raspberry Pi Pico W
  SG1 = Buzzer 12mm [part_number=COM-07950 package=buzzer-12mm-ns]

nets:
  N1: A1.pin_31, SG1.1
  N2: A1.pin_33, A1.pin_42, SG1.2

notes:
  buzzer between
  pin 26 and ground

custom parts:
  Raspberry Pi Pico W: Raspberry Pi Pico W. Based around the RP2040 microcontroller the Pico W is a low cost microcontroller device bringing Raspberry Pi quality, cost, and easy of use to the microcontroller space. The areas marked KEEPOUT in pcb silkscreen should not have traces running through them to avoid shorts on a soldered in module!
  Buzzer 12mm: Buzzer 12mm Spark Fun Electronics SKU : Comp-Buzzer Through hole This is a small 12mm round speaker that operates around the audible 2kHz range. You can use these speakers to create simple music or user interfaces. This is not a true piezoelectric speaker but behaves similarly. Instead of a piezoelectric crystal that vibrates with an electric current, this tiny speaker uses an electromagnet to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
