# Fritzing sketch LilyPicoWFritzButton (saved by Fritzing 0.9.10b)
breadboards: 2

parts:
  A1 = Raspberry Pi Pico W
  R1 = Resistor [tolerance=±5% resistance=220 package="2512 [SMD]"]
  S1 = Pushbutton [package="[THT]"]
  LED1 = LED - 5mm [color="Red (633nm)" current=0.030 package="5 mm [THT]"]

nets:
  N1: A1.pin_29, R1.Pin_1
  N2: A1.pin_31, S1.Pin_1, S1.Pin_2
  N3: A1.pin_34, LED1.anode
  N4: A1.pin_36, S1.Pin_3, S1.Pin_4
  N5: R1.Pin_0, LED1.cathode

notes:
  Button between
  pin 26 and 3.3V
  LED between pin 28, resistor and ground

custom parts:
  Raspberry Pi Pico W: Raspberry Pi Pico W. Based around the RP2040 microcontroller the Pico W is a low cost microcontroller device bringing Raspberry Pi quality, cost, and easy of use to the microcontroller space. The areas marked KEEPOUT in pcb silkscreen should not have traces running through them to avoid shorts on a soldered in module!
