# Fritzing sketch LilyPicoWFritzExternalLED (saved by Fritzing 0.9.10b)
breadboards: 2

parts:
  A1 = Raspberry Pi Pico W
  R1 = Resistor [tolerance=±5% resistance=220 package="2512 [SMD]"]
  LED1 = LED - 5mm [color="Red (633nm)" current=0.030 package="5 mm [THT]"]

nets:
  N1: A1.pin_29, R1.Pin_1
  N2: A1.pin_34, LED1.anode
  N3: R1.Pin_0, LED1.cathode

notes:
  LED between pin 28, 220 ohm resistor and ground

custom parts:
  Raspberry Pi Pico W: Raspberry Pi Pico W. Based around the RP2040 microcontroller the Pico W is a low cost microcontroller device bringing Raspberry Pi quality, cost, and easy of use to the microcontroller space. The areas marked KEEPOUT in pcb silkscreen should not have traces running through them to avoid shorts on a soldered in module!
