# Fritzing sketch LilyPicoWFritzMotors (saved by Fritzing 0.9.10b)
breadboards: 2

parts:
  A1 = Raspberry Pi Pico W
  Part1 = Adafruit TB6612 DC and Stepper Motor Driver [part_number="Adafruit #2448"]
  M1 = gear-motor
  M2 = gear-motor

nets:
  N1: A1.pin_26, Part1.PWMB
  N2: A1.pin_27, Part1.BIN2
  N3: A1.pin_29, Part1.BIN1
  N4: A1.pin_31, Part1.AIN1
  N5: A1.pin_32, Part1.AIN2
  N6: A1.pin_34, Part1.PWMA
  N7: A1.pin_38, A1.pin_42, Part1.GND
  N8: A1.pin_40, Part1.PWRIN, Part1.VCC
  N9: Part1.MOTORA1, M2.pin_2
  N10: Part1.MOTORA2, M2.pin_1
  N11: Part1.MOTORB2, M1.pin_2
  N12: Part1.MOTORB1, M1.pin_1

notes:
  VIN-5V
  VM-5V
  PWMA-Pin 28
  AIN2 -Pin 27
  AIN1-Pin 26
  BIN1-Pin 22
  BIN2-Pin 21
  PWMB-Pin 20
  GND-ground
  Right Motor
  Left Motor

custom parts:
  Raspberry Pi Pico W: Raspberry Pi Pico W. Based around the RP2040 microcontroller the Pico W is a low cost microcontroller device bringing Raspberry Pi quality, cost, and easy of use to the microcontroller space. The areas marked KEEPOUT in pcb silkscreen should not have traces running through them to avoid shorts on a soldered in module!
  Adafruit TB6612 DC and Stepper Motor Driver: Spin two DC motors, step one bi-polar or uni-polar stepper, or fire off two solenoids with 1.2A per channel using the TB6612. These are perhaps better known as "the drivers in our assembled Adafruit Motorshield or Motor HAT." We really like these dual H-bridges, so if you want to control motors without a shield or HAT these are easy to include on any solderless breadboard or perma-proto.
