# Fritzing sketch LilyPicoWFritzOA (saved by Fritzing 0.9.10b)
breadboards: 2

parts:
  A1 = Raspberry Pi Pico W
  Part1 = Adafruit TB6612 DC and Stepper Motor Driver [part_number="Adafruit #2448"]
  M1 = gear-motor
  M2 = gear-motor
  HC-SR04_Sensor_1 = HC-SR04 Ultrasonic Distance Sensor
  LED1 = smd LED [color="Red (633nm)" package="1206 [SMD]"]
  R1 = Resistor [tolerance=±5% resistance=220 package="2512 [SMD]"]

nets:
  GND: A1.pin_18, A1.pin_23, A1.pin_38, A1.pin_42, Part1.GND, HC-SR04_Sensor_1.GND, R1.Pin_1
  N1: A1.pin_21, HC-SR04_Sensor_1.ECHO
  N2: A1.pin_22, HC-SR04_Sensor_1.TRIG
  N3: A1.pin_24, LED1.anode
  N4: A1.pin_26, Part1.PWMB
  N5: A1.pin_27, Part1.BIN2
  N6: A1.pin_29, Part1.BIN1
  N7: A1.pin_31, Part1.AIN1
  N8: A1.pin_32, Part1.AIN2
  N9: A1.pin_34, Part1.PWMA
  N10: A1.pin_36, HC-SR04_Sensor_1.VCC
  N11: A1.pin_40, Part1.PWRIN, Part1.VCC
  N12: Part1.MOTORA1, M2.pin_2
  N13: Part1.MOTORA2, M2.pin_1
  N14: Part1.MOTORB2, M1.pin_2
  N15: Part1.MOTORB1, M1.pin_1
  N16: LED1.cathode, R1.Pin_0

notes:
  Left motor
  right motor
  Sonar
  VCC - 3.3V out
  Trig - pin 17
  Echo - pin 16
  GND - ground
  VIN-5V
  VM-5V
  PWMA-Pin 28
  AIN2 -Pin 27
  AIN1-Pin 26
  BIN1-Pin 22
  BIN2-Pin 21
  PWMB-Pin 20
  GND-ground
  LED between
  pin 18, 220 ohm resistor and ground

custom parts:
  Raspberry Pi Pico W: Raspberry Pi Pico W. Based around the RP2040 microcontroller the Pico W is a low cost microcontroller device bringing Raspberry Pi quality, cost, and easy of use to the microcontroller space. The areas marked KEEPOUT in pcb silkscreen should not have traces running through them to avoid shorts on a soldered in module!
  Adafruit TB6612 DC and Stepper Motor Driver: Spin two DC motors, step one bi-polar or uni-polar stepper, or fire off two solenoids with 1.2A per channel using the TB6612. These are perhaps better known as "the drivers in our assembled Adafruit Motorshield or Motor HAT." We really like these dual H-bridges, so if you want to control motors without a shield or HAT these are easy to include on any solderless breadboard or perma-proto.
