# Fritzing sketch LilyPicoWFritzPot (saved by Fritzing 0.9.10b)
breadboards: 2

parts:
  A1 = Raspberry Pi Pico W
  LED1 = LED - 5mm [color="Red (633nm)" current=0.030 package="5 mm [THT]"]
  R1 = Resistor [tolerance=±5% resistance=220 package="0805 [SMD]"]
  U3 = POT [knob_status=50% power=0.5W package=pot_alpha_rv16af-20]

nets:
  N1: A1.pin_28, A1.pin_42, U3.E
  N2: A1.pin_32, U3.S
  N3: A1.pin_34, LED1.anode
  N4: A1.pin_40, U3.A
  N5: LED1.cathode, R1.Pin_1

notes:
  LED between pin 28, 220 ohm resistor and ground
  potentiometer between 5V, pin 27 and ground

custom parts:
  Raspberry Pi Pico W: Raspberry Pi Pico W. Based around the RP2040 microcontroller the Pico W is a low cost microcontroller device bringing Raspberry Pi quality, cost, and easy of use to the microcontroller space. The areas marked KEEPOUT in pcb silkscreen should not have traces running through them to avoid shorts on a soldered in module!
