# Fritzing sketch LilyPicoWFritzSwitch (saved by Fritzing 0.9.10b)
breadboards: 2

parts:
  A1 = Raspberry Pi Pico W
  LED1 = LED - 5mm [color="Red (633nm)" current=0.030 package="5 mm [THT]"]
  R1 = Resistor [tolerance=±5% resistance=220 package="0805 [SMD]"]
  S3 = Toggle Switch [package=THT]

nets:
  N1: A1.pin_31, S3.COM
  N2: A1.pin_33, A1.pin_42, S3.L1
  N3: A1.pin_34, LED1.anode
  N4: LED1.cathode, R1.Pin_1

custom parts:
  Raspberry Pi Pico W: Raspberry Pi Pico W. Based around the RP2040 microcontroller the Pico W is a low cost microcontroller device bringing Raspberry Pi quality, cost, and easy of use to the microcontroller space. The areas marked KEEPOUT in pcb silkscreen should not have traces running through them to avoid shorts on a soldered in module!
