# Fritzing sketch LilyPicoWSonarLED (saved by Fritzing 0.9.10b)
breadboards: 2

parts:
  A1 = Raspberry Pi Pico W
  LED1 = LED - 5mm [color="Red (633nm)" current=0.030 package="5 mm [THT]"]
  R1 = Resistor [tolerance=±5% resistance=220 package="0805 [SMD]"]
  HC-SR04_Sensor_1 = HC-SR04 Ultrasonic Distance Sensor

nets:
  N1: A1.pin_3, A1.pin_33, A1.pin_42, R1.Pin_0, HC-SR04_Sensor_1.GND
  N2: A1.pin_4, HC-SR04_Sensor_1.ECHO
  N3: A1.pin_5, HC-SR04_Sensor_1.TRIG
  N4: A1.pin_34, LED1.anode
  N5: A1.pin_36, HC-SR04_Sensor_1.VCC
  N6: LED1.cathode, R1.Pin_1

notes:
  Sonar
  VCC - 3.3V out
  Trig - pin 3
  Echo - pin 2
  GND - ground
  LED between
  pin 28, 220 ohm resistor and ground

custom parts:
  Raspberry Pi Pico W: Raspberry Pi Pico W. Based around the RP2040 microcontroller the Pico W is a low cost microcontroller device bringing Raspberry Pi quality, cost, and easy of use to the microcontroller space. The areas marked KEEPOUT in pcb silkscreen should not have traces running through them to avoid shorts on a soldered in module!
